// Logisim project Task 3 flip flop.circ as structural Verilog: 1 circuit, main circuit main
module main (
);

  wire button_1_out, clock_1_out, nand_1_out, nand_2_out, nand_3_out, nand_4_out, not_1_out;

  Button button_1 (.out(button_1_out));
  Clock clock_1 (.out(clock_1_out));
  not not_1 (not_1_out, button_1_out);
  not nand_1 (nand_1_out, clock_1_out);  // NAND_Gate
  nand nand_2 (nand_2_out, not_1_out, clock_1_out);
  not nand_3 (nand_3_out, nand_4_out);  // NAND_Gate
  nand nand_4 (nand_4_out, nand_3_out, nand_2_out);
  LED led_1 (.in(nand_4_out));
  LED led_2 (.in(nand_3_out));
  // also tied to GND on the sheet: nand_3_out
endmodule
